// Logisim project cpu.circ as structural Verilog
module alu (
  input  [15:0] in_1,
  input  [15:0] in_2,
  input  [2:0] in_3,
  output [15:0] out_4
);

  wire [15:0] adder_1_out, nand_1_out, negator_1_out, shifter_1_out, shifter_2_out, subtractor_1_out;

  Shifter #(.width(16), .shift("lr")) shifter_1 (.in(in_1), .\dist (4'b0001), .out(shifter_1_out));
  Shifter #(.width(16)) shifter_2 (.in(in_1), .\dist (4'b0001), .out(shifter_2_out));
  Adder #(.width(16)) adder_1 (.a(in_1), .b(in_2), .out(adder_1_out), .cin(1'b0));  // open: cout
  Subtractor #(.width(16)) subtractor_1 (.a(in_1), .b(in_2), .out(subtractor_1_out), .bin(1'b0));  // open: bout
  assign nand_1_out = ~(in_1 & in_2);  // NAND_Gate nand_1, 16 bits wide
  Negator #(.width(16)) negator_1 (.in(in_1), .out(negator_1_out));
  Multiplexer #(.select(3), .width(16), .enable("false")) multiplexer_1 (
    .in0(shifter_1_out), .in1(shifter_2_out), .in2(adder_1_out), .in3(subtractor_1_out), .in4(nand_1_out),
    .in5(negator_1_out), .in6({16{1'b0}}), .in7(16'h1), .out(out_4), .sel(in_3));

  // Notes on the sheet:
  //   Source
  //   Destination
endmodule

// Regs
module register_bank (
  input  WEn,
  input  [15:0] DstIn,
  input  Clk,
  input  [2:0] DstSel,
  input  [2:0] SrcSel,
  output [15:0] DstOut,
  output [15:0] SrcOut,
  output [15:0] IP,
  output [15:0] SP
);

  wire demultiplexer_1_out0, demultiplexer_1_out1, demultiplexer_1_out2, demultiplexer_1_out3,
       demultiplexer_1_out4, demultiplexer_1_out5, demultiplexer_1_out6, demultiplexer_1_out7, not_1_out;
  wire [15:0] register_1_q, register_2_q, register_3_q, register_4_q, register_5_q, register_6_q;

  not not_1 (not_1_out, WEn);
  Demultiplexer #(.select(3)) demultiplexer_1 (
    .out0(demultiplexer_1_out0), .out1(demultiplexer_1_out1), .out2(demultiplexer_1_out2),
    .out3(demultiplexer_1_out3), .out4(demultiplexer_1_out4), .out5(demultiplexer_1_out5),
    .out6(demultiplexer_1_out6), .out7(demultiplexer_1_out7), .in(not_1_out), .sel(DstSel));  // open: en
  Multiplexer #(.select(3), .width(16)) multiplexer_1 (
    .in0(IP), .in1(SP), .in2(register_1_q), .in3(register_2_q), .in4(register_3_q), .in5(register_4_q),
    .in6(register_5_q), .in7(register_6_q), .out(DstOut), .sel(DstSel));  // open: en
  Register #(.width(16)) u_IP (.D(DstIn), .en(demultiplexer_1_out0), .Q(IP), .clk(Clk));  // open: clr
  Multiplexer #(.select(3), .width(16)) multiplexer_2 (
    .in0(IP), .in1(SP), .in2(register_1_q), .in3(register_2_q), .in4(register_3_q), .in5(register_4_q),
    .in6(register_5_q), .in7(register_6_q), .out(SrcOut), .sel(SrcSel));  // open: en
  Register #(.width(16)) u_SP (.D(DstIn), .en(demultiplexer_1_out1), .Q(SP), .clk(Clk));  // open: clr
  Register #(.width(16)) register_1 (.D(DstIn), .en(demultiplexer_1_out2), .Q(register_1_q), .clk(Clk));  // open: clr
  Register #(.width(16)) register_2 (.D(DstIn), .en(demultiplexer_1_out3), .Q(register_2_q), .clk(Clk));  // open: clr
  Register #(.width(16)) register_3 (.D(DstIn), .en(demultiplexer_1_out4), .Q(register_3_q), .clk(Clk));  // open: clr
  Register #(.width(16)) register_4 (.D(DstIn), .en(demultiplexer_1_out5), .Q(register_4_q), .clk(Clk));  // open: clr
  Register #(.width(16)) register_5 (.D(DstIn), .en(demultiplexer_1_out6), .Q(register_5_q), .clk(Clk));  // open: clr
  Register #(.width(16)) register_6 (.D(DstIn), .en(demultiplexer_1_out7), .Q(register_6_q), .clk(Clk));  // open: clr
endmodule

// Ctrl
module cpu_controller (
  input  [15:0] IP,
  input  [15:0] Inst,
  output Clk,
  output RegsWEn,
  output [2:0] SrcSel,
  output [2:0] DstSel,
  output [3:0] AluOp,
  output [1:0] MemCtrl,
  output [15:0] Addr,
  output MemClk
);

  Register #(.width(16)) register_1 (.D(Inst));  // open: en, Q, clk, clr
  Register #(.width(16)) register_2 (.D(Inst));  // open: en, Q, clk, clr

  assign Addr = IP;
endmodule

module cpu (
  input  Clk,
  output [15:0] InstData,
  output [15:0] InstAddr,
  output [15:0] DataData,
  output InstClk,
  output [15:0] DataAddr,
  output [1:0] DataCtrl
);

  wire not_1_out;
  wire [15:0] alu_1_out_4, register_bank_1_dstout, register_bank_1_ip;

  not not_1 (not_1_out, Clk);
  register_bank register_bank_1 (
    .DstIn(DataData), .Clk(not_1_out), .DstOut(register_bank_1_dstout), .SrcOut(DataAddr),
    .IP(register_bank_1_ip));  // open: WEn, DstSel, SrcSel, SP
  alu alu_1 (.in_1(DataAddr), .in_2(register_bank_1_dstout), .out_4(alu_1_out_4));  // open: in_3
  Controlled_Buffer #(.width(16)) controlled_buffer_1 (.in(register_bank_1_dstout), .out(DataData));  // open: en
  Controlled_Buffer #(.width(16)) controlled_buffer_2 (.in(alu_1_out_4), .out(DataData));  // open: en
  Pull_Resistor pull_resistor_1 (.node(DataAddr));
  Pull_Resistor pull_resistor_2 (.node(DataData));

  // Notes on the sheet:
  //   DataBus
  //   AddressBus
endmodule
